# Fritzing sketch CO2_Sensor (saved by Fritzing 0.9.4)

parts:
  Buzzer = Piezo Speaker
  NodeMCU_Lolin_V3 = ESP8266 NodeMCU LoLin module
  Joy-It_CCS811 = Adafruit CCS811 [part_number="Adafruit #3566"]
  P1 = SK6812 RGBW RGB LED
  P2 = SK6812 RGBW RGB LED

nets:
  GND: Buzzer.pin1, NodeMCU_Lolin_V3.GND, Joy-It_CCS811.GND, P2.VSS#5
  N1: Buzzer.pin2, NodeMCU_Lolin_V3.D7
  N2: NodeMCU_Lolin_V3.D0, NodeMCU_Lolin_V3.RST
  N3: NodeMCU_Lolin_V3.D1, Joy-It_CCS811.SCL
  N4: NodeMCU_Lolin_V3.D2, Joy-It_CCS811.SDA, Joy-It_CCS811.!INT
  3V3: NodeMCU_Lolin_V3.3V3, Joy-It_CCS811.VCC, Joy-It_CCS811.3.3V
  N5: NodeMCU_Lolin_V3.D5, Joy-It_CCS811.!WAKE
  N6: NodeMCU_Lolin_V3.D6, P2.DIN
  N7: NodeMCU_Lolin_V3.VU, P2.VDD#1
  N8: P1.VDD, P2.VDD#2
  N9: P1.DIN, P2.DOUT
  N10: P1.VSS, P2.VSS#6

custom parts:
  ESP8266 NodeMCU LoLin module: ESP8266 based NodeMCU
  Adafruit CCS811: Breathe easy - we finally have an I2C VOC/eCO2 sensor in the Adafruit shop! Add air quality monitoring to your project and with an Adafruit CCS811 Air Quality Sensor Breakout. This sensor from AMS is a gas sensor that can detect a wide range of Volatile Organic Compounds (VOCs) and is intended for indoor air quality monitoring. When connected to your microcontroller (running our library code)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
  SK6812 RGBW RGB LED: These have no mounting holes or soldering vias…wires must be soldered directly to pads on the back of the PCB. Each is about 10 millimeters (0.3 inches) in diameter. These are RGB only; there’s no RGBW version.
